# Fritzing sketch led_driver_circuit (saved by Fritzing 0.7.12b)
breadboards: 1

parts:
  STP08DP1 = STP08DP05 [chip_label=STP08DP05 package="DIP (Dual Inline) [THT]"]
  R1 = Resistor [tolerance=±5% resistance=220 package=THT]
  LED0 = LED - 5mm [color="Red (633nm)" package="5 mm [THT]"]
  LED2 = LED - 5mm [color="Red (633nm)" package="5 mm [THT]"]  # not connected
  LED4 = LED - 5mm [color="Red (633nm)" package="5 mm [THT]"]  # not connected
  LED6 = LED - 5mm [color="Red (633nm)" package="5 mm [THT]"]  # not connected
  LED1 = LED - 5mm [color="Green (565nm)" package="5 mm [THT]"]
  LED3 = LED - 5mm [color="Green (565nm)" package="5 mm [THT]"]  # not connected
  LED5 = LED - 5mm [color="Green (565nm)" package="5 mm [THT]"]  # not connected
  LED7 = LED - 5mm [color="Green (565nm)" package="5 mm [THT]"]  # not connected

nets:
  N1: STP08DP1.GND, STP08DP1.OE, R1.Pin_0
  N2: STP08DP1.0, LED0.cathode
  N3: STP08DP1.1, LED1.cathode
  N4: STP08DP1.Rext, R1.Pin_1
  N5: STP08DP1.VCC, LED0.anode, LED1.anode

notes:
  VCC
  GND
  SDI
  CLK
  LCH
  To next board

custom parts:
  STP08DP05: Power shift register.
