# Fritzing sketch led_driver_pcb (saved by Fritzing 0.7.12b)
breadboards: 1

parts:
  STP08DP1 = STP08DP05 [chip_label=STP08DP05 package="DIP (Dual Inline) [THT]"]
  R1 = Resistor [tolerance=±5% resistance=220 package=THT]
  DC_Power1 = DC Power [voltage=5]
  J8 = female pin header, 1 pin [form="♀ (female)"]
  J9 = female pin header, 1 pin [form="♀ (female)"]
  J10 = female pin header, 6 pins [form="♀ (female)"]
  J11 = female pin header, 4 pins [form="♀ (female)"]
  J12 = female pin header, 8 pins [form="♀ (female)"]
  J14 = female pin header, 6 pins [form="♀ (female)"]
  J13 = female pin header, 1 pin [form="♀ (female)"]

nets:
  GND: STP08DP1.GND, STP08DP1.OE, R1.Pin_0, J10.pin2, J12.pin1, J13.pin1
  N1: STP08DP1.SDI, J12.pin2
  N2: STP08DP1.CLK, J12.pin3, J14.pin1
  N3: STP08DP1.LCH, J12.pin4, J14.pin2
  N4: STP08DP1.0, J12.pin5
  N5: STP08DP1.1, J12.pin6
  N6: STP08DP1.2, J12.pin7
  N7: STP08DP1.3, J12.pin8
  N8: STP08DP1.4, J10.pin6
  N9: STP08DP1.5, J10.pin5
  N10: STP08DP1.6, J10.pin4
  N11: STP08DP1.7, J10.pin3
  N12: STP08DP1.SDO, J10.pin1
  N13: STP08DP1.Rext, R1.Pin_1
  N14: STP08DP1.VCC, DC_Power1.V+, J8.pin1, J9.pin1, J11.pin1, J11.pin2, J11.pin3, J11.pin4, J14.pin3, J14.pin4, J14.pin5, J14.pin6

notes:
  VCC
  GND
  SDI
  CLK
  LCH
  To next board
  @onyxfish
  SDO
  OE
  L0
  L1
  L2
  L3
  L4
  L5
  L6
  L7
  R1
  STP08DP05 breakout

custom parts:
  STP08DP05: Power shift register.
